// Logisim project main.circ as structural Verilog: 11 circuits, main circuit Display
module Display (
  input  D,
  input  C,
  input  B,
  input  A,
  output a_2,
  output b_2,
  output c_2,
  output d_2,
  output e,
  output f,
  output g
);

  wire nand_1_out, nand_2_out, nand_3_out, nand_4_out, nand_5_out, nand_6_out, nand_7_out, nand_8_out,
       nand_9_out, nand_10_out, nand_11_out, nand_12_out, nand_13_out, nand_14_out, nand_15_out, nand_16_out,
       nand_17_out, nand_18_out, nand_19_out, nand_20_out, nand_21_out, nand_22_out, nand_23_out,
       nand_24_out, nand_25_out, nand_26_out, nand_27_out, nand_28_out, nand_29_out, nand_30_out,
       nand_31_out, nand_32_out, nand_33_out, nand_34_out, nand_35_out, nand_36_out, nand_37_out,
       nand_38_out, nand_39_out, nand_40_out, nand_41_out, nand_42_out, nand_43_out, nand_44_out,
       nand_45_out, nand_46_out, nand_47_out, nand_48_out, nand_49_out, nand_50_out, nand_51_out,
       nand_52_out, nand_53_out, nand_54_out, nand_55_out, nand_56_out, nand_57_out, nand_58_out,
       nand_59_out, nand_60_out, nand_61_out, nand_62_out, nand_63_out, nand_64_out, nand_65_out,
       nand_66_out, nand_67_out, nand_68_out, nand_69_out, nand_70_out, nand_71_out, nand_72_out,
       nand_73_out, nand_74_out, nand_75_out, nand_76_out, nand_77_out, nand_78_out, nand_79_out,
       nand_80_out, nand_81_out, nand_82_out, nand_83_out, nand_84_out, nand_85_out, nand_86_out,
       nand_87_out, nand_88_out, nand_89_out, nand_90_out, nand_91_out, nand_92_out, nand_93_out,
       nand_94_out, nand_95_out, nand_96_out, nand_97_out, nand_98_out, nand_99_out, nand_100_out,
       nand_101_out, nand_102_out, nand_103_out, nand_104_out, nand_106_out, nand_107_out, nand_108_out,
       nand_109_out, nand_110_out, nand_111_out, nand_112_out, nand_113_out, nand_114_out, nand_115_out,
       nand_116_out, nand_117_out, nand_118_out, nand_119_out, nand_120_out, nand_121_out, nand_122_out,
       nand_123_out, nand_124_out, nand_125_out, nand_126_out, nand_127_out, nand_128_out, nand_129_out,
       nand_130_out, nand_131_out, nand_132_out, nand_133_out, nand_134_out, nand_136_out, nand_137_out,
       nand_138_out, nand_139_out, nand_141_out, nand_142_out, nand_143_out, nand_144_out, nand_145_out,
       nand_146_out, nand_147_out, nand_148_out;

  nand nand_1 (nand_1_out, C, C);
  nand nand_2 (nand_2_out, D, D);
  nand nand_3 (nand_3_out, B, B);
  nand nand_4 (nand_4_out, D, D);
  nand nand_5 (nand_5_out, B, B);
  nand nand_6 (nand_6_out, D, D);
  nand nand_7 (nand_7_out, D, D);
  nand nand_8 (nand_8_out, C, C);
  nand nand_9 (nand_9_out, C, C);
  nand nand_10 (nand_10_out, C, C);
  nand nand_11 (nand_11_out, A, A);
  nand nand_12 (nand_12_out, A, A);
  nand nand_13 (nand_13_out, D, D);
  nand nand_14 (nand_14_out, C, C);
  nand nand_15 (nand_15_out, A, A);
  nand nand_16 (nand_16_out, D, D);
  nand nand_17 (nand_17_out, D, nand_1_out);
  nand nand_18 (nand_18_out, nand_2_out, nand_3_out);
  nand nand_19 (nand_19_out, nand_4_out, nand_5_out);
  nand nand_20 (nand_20_out, nand_6_out, A);
  nand nand_21 (nand_21_out, nand_7_out, nand_8_out);
  nand nand_22 (nand_22_out, nand_9_out, B);
  nand nand_23 (nand_23_out, nand_10_out, nand_11_out);
  nand nand_24 (nand_24_out, B, nand_12_out);
  nand nand_25 (nand_25_out, D, B);
  nand nand_26 (nand_26_out, D, C);
  nand nand_27 (nand_27_out, nand_13_out, C);
  nand nand_28 (nand_28_out, nand_14_out, B);
  nand nand_29 (nand_29_out, B, nand_15_out);
  nand nand_30 (nand_30_out, nand_16_out, C);
  nand nand_31 (nand_31_out, C, C);
  nand nand_32 (nand_32_out, A, A);
  nand nand_33 (nand_33_out, D, D);
  nand nand_34 (nand_34_out, D, D);
  nand nand_35 (nand_35_out, nand_17_out, nand_17_out);
  nand nand_36 (nand_36_out, B, B);
  nand nand_37 (nand_37_out, D, D);
  nand nand_38 (nand_38_out, C, C);
  nand nand_39 (nand_39_out, nand_18_out, nand_18_out);
  nand nand_40 (nand_40_out, A, A);
  nand nand_41 (nand_41_out, D, D);
  nand nand_42 (nand_42_out, B, B);
  nand nand_43 (nand_43_out, nand_19_out, nand_20_out);
  nand nand_44 (nand_44_out, B, B);
  nand nand_45 (nand_45_out, D, D);
  nand nand_46 (nand_46_out, C, C);
  nand nand_47 (nand_47_out, nand_21_out, nand_21_out);
  nand nand_48 (nand_48_out, A, A);
  nand nand_49 (nand_49_out, nand_22_out, nand_22_out);
  nand nand_50 (nand_50_out, B, B);
  nand nand_51 (nand_51_out, B, B);
  nand nand_52 (nand_52_out, nand_23_out, nand_24_out);
  nand nand_53 (nand_53_out, nand_25_out, nand_26_out);
  nand nand_54 (nand_54_out, B, B);
  nand nand_55 (nand_55_out, A, A);
  nand nand_56 (nand_56_out, nand_27_out, nand_27_out);
  nand nand_57 (nand_57_out, B, B);
  nand nand_58 (nand_58_out, nand_28_out, nand_29_out);
  nand nand_59 (nand_59_out, nand_30_out, nand_30_out);
  nand nand_60 (nand_60_out, B, B);
  nand nand_61 (nand_61_out, C, C);
  nand nand_62 (nand_62_out, nand_31_out, nand_32_out);
  nand nand_63 (nand_63_out, nand_33_out, B);
  nand nand_64 (nand_64_out, nand_34_out, C);
  nand nand_65 (nand_65_out, C, B);
  nand nand_66 (nand_66_out, nand_35_out, nand_36_out);
  nand nand_67 (nand_67_out, nand_37_out, nand_38_out);
  nand nand_68 (nand_68_out, nand_39_out, nand_40_out);
  nand nand_69 (nand_69_out, nand_41_out, B);
  nand nand_70 (nand_70_out, D, nand_42_out);
  nand nand_71 (nand_71_out, nand_43_out, nand_43_out);
  nand nand_72 (nand_72_out, nand_44_out, A);
  nand nand_73 (nand_73_out, nand_45_out, C);
  nand nand_74 (nand_74_out, D, nand_46_out);
  nand nand_75 (nand_75_out, nand_47_out, nand_48_out);
  nand nand_76 (nand_76_out, nand_49_out, A);
  nand nand_77 (nand_77_out, C, nand_50_out);
  nand nand_78 (nand_78_out, C, B);
  nand nand_79 (nand_79_out, D, nand_51_out);
  nand nand_80 (nand_80_out, nand_52_out, nand_52_out);
  nand nand_81 (nand_81_out, nand_53_out, nand_53_out);
  nand nand_82 (nand_82_out, nand_54_out, nand_55_out);
  nand nand_83 (nand_83_out, nand_56_out, nand_57_out);
  nand nand_84 (nand_84_out, nand_58_out, nand_58_out);
  nand nand_85 (nand_85_out, nand_59_out, nand_60_out);
  nand nand_86 (nand_86_out, D, nand_61_out);
  nand nand_87 (nand_87_out, D, A);
  nand nand_88 (nand_88_out, nand_62_out, nand_63_out);
  nand nand_89 (nand_89_out, nand_64_out, nand_64_out);
  nand nand_90 (nand_90_out, nand_65_out, nand_66_out);
  nand nand_91 (nand_91_out, A, A);
  nand nand_92 (nand_92_out, nand_67_out, nand_68_out);
  nand nand_93 (nand_93_out, C, C);
  nand nand_94 (nand_94_out, A, A);
  nand nand_95 (nand_95_out, nand_69_out, nand_69_out);
  nand nand_96 (nand_96_out, nand_70_out, nand_70_out);
  nand nand_97 (nand_97_out, nand_71_out, nand_72_out);
  nand nand_98 (nand_98_out, nand_73_out, nand_74_out);
  nand nand_99 (nand_99_out, nand_75_out, nand_76_out);
  nand nand_100 (nand_100_out, nand_77_out, nand_77_out);
  nand nand_101 (nand_101_out, nand_78_out, nand_78_out);
  nand nand_102 (nand_102_out, A, A);
  nand nand_103 (nand_103_out, nand_79_out, nand_79_out);
  nand nand_104 (nand_104_out, A, A);
  nand nand_105 (e, nand_80_out, nand_81_out);
  nand nand_106 (nand_106_out, nand_82_out, nand_83_out);
  nand nand_107 (nand_107_out, A, A);
  nand nand_108 (nand_108_out, C, C);
  nand nand_109 (nand_109_out, nand_84_out, nand_85_out);
  nand nand_110 (nand_110_out, nand_86_out, nand_87_out);
  nand nand_111 (nand_111_out, nand_88_out, nand_88_out);
  nand nand_112 (nand_112_out, nand_89_out, A);
  nand nand_113 (nand_113_out, nand_90_out, nand_90_out);
  nand nand_114 (nand_114_out, D, nand_91_out);
  nand nand_115 (nand_115_out, nand_92_out, nand_92_out);
  nand nand_116 (nand_116_out, nand_93_out, nand_94_out);
  nand nand_117 (nand_117_out, nand_95_out, A);
  nand nand_118 (nand_118_out, nand_96_out, A);
  nand nand_119 (nand_119_out, nand_97_out, nand_97_out);
  nand nand_120 (nand_120_out, nand_98_out, nand_98_out);
  nand nand_121 (nand_121_out, nand_99_out, nand_99_out);
  nand nand_122 (nand_122_out, nand_100_out, A);
  nand nand_123 (nand_123_out, nand_101_out, nand_102_out);
  nand nand_124 (nand_124_out, nand_103_out, nand_104_out);
  nand nand_125 (nand_125_out, nand_106_out, nand_106_out);
  nand nand_126 (nand_126_out, C, nand_107_out);
  nand nand_127 (nand_127_out, D, nand_108_out);
  nand nand_128 (nand_128_out, D, B);
  nand nand_129 (nand_129_out, nand_109_out, nand_109_out);
  nand nand_130 (nand_130_out, nand_110_out, nand_110_out);
  nand nand_131 (nand_131_out, nand_111_out, nand_112_out);
  nand nand_132 (nand_132_out, nand_113_out, nand_114_out);
  nand nand_133 (nand_133_out, nand_115_out, nand_116_out);
  nand nand_134 (nand_134_out, nand_117_out, nand_118_out);
  nand nand_135 (c_2, nand_119_out, nand_120_out);
  nand nand_136 (nand_136_out, nand_121_out, nand_122_out);
  nand nand_137 (nand_137_out, nand_123_out, nand_124_out);
  nand nand_138 (nand_138_out, nand_125_out, nand_126_out);
  nand nand_139 (nand_139_out, nand_127_out, nand_128_out);
  nand nand_140 (g, nand_129_out, nand_130_out);
  nand nand_141 (nand_141_out, nand_131_out, nand_131_out);
  nand nand_142 (nand_142_out, nand_132_out, nand_132_out);
  nand nand_143 (nand_143_out, nand_133_out, nand_133_out);
  nand nand_144 (nand_144_out, nand_134_out, nand_134_out);
  nand nand_145 (nand_145_out, nand_136_out, nand_136_out);
  nand nand_146 (nand_146_out, nand_137_out, nand_137_out);
  nand nand_147 (nand_147_out, nand_138_out, nand_138_out);
  nand nand_148 (nand_148_out, nand_139_out, nand_139_out);
  nand nand_149 (a_2, nand_141_out, nand_142_out);
  nand nand_150 (b_2, nand_143_out, nand_144_out);
  nand nand_151 (d_2, nand_145_out, nand_146_out);
  nand nand_152 (f, nand_147_out, nand_148_out);
endmodule

module BC (
  input  Enable,
  input  Input,
  input  Clock,
  input  R___W,
  output Output
);

  wire and_1_out, and_2_out, not_1_out, not_2_out, s_r_ff_1_q;

  not not_1 (not_1_out, Input);
  not not_2 (not_2_out, R___W);
  and and_1 (and_1_out, Enable, not_1_out, not_2_out);
  and and_2 (and_2_out, Input, Enable, not_2_out);
  S_R_Flip_Flop s_r_ff_1 (.S(and_2_out), .clk(Clock), .R(and_1_out), .Q(s_r_ff_1_q));  // open: Qn, preset, reset, en
  and and_3 (Output, s_r_ff_1_q, Enable, R___W);
endmodule

module _4x4 (
  input  I0,
  input  I1,
  input  I2,
  input  I3,
  input  E,
  input  [1:0] Addr,
  input  R_W,
  output O0,
  output O1,
  output O2,
  output O3
);

  wire bc_1_output, bc_2_output, bc_3_output, bc_4_output, bc_5_output, bc_6_output, bc_7_output,
       bc_8_output, bc_9_output, bc_10_output, bc_11_output, bc_12_output, bc_13_output, bc_14_output,
       bc_15_output, bc_16_output, clock_1_out, decoder_1_out0, decoder_1_out1, decoder_1_out2,
       decoder_1_out3, or_1_out, or_2_out, or_3_out, or_4_out;

  Decoder #(.select(2)) decoder_1 (
    .out0(decoder_1_out0), .out1(decoder_1_out1), .out2(decoder_1_out2), .out3(decoder_1_out3), .sel(Addr),
    .en(E));
  Clock clock_1 (.out(clock_1_out));
  BC bc_1 (.Input(I0), .Clock(clock_1_out), .Enable(decoder_1_out0), .R___W(R_W), .Output(bc_1_output));
  BC bc_2 (.Input(I0), .Clock(clock_1_out), .Enable(decoder_1_out1), .R___W(R_W), .Output(bc_2_output));
  BC bc_3 (.Input(I0), .Clock(clock_1_out), .Enable(decoder_1_out2), .R___W(R_W), .Output(bc_3_output));
  BC bc_4 (.Input(I0), .Clock(clock_1_out), .Enable(decoder_1_out3), .R___W(R_W), .Output(bc_4_output));
  or or_1 (or_1_out, bc_3_output, bc_2_output, bc_1_output, bc_4_output);
  BC bc_5 (.Input(I1), .Clock(clock_1_out), .Enable(decoder_1_out0), .R___W(R_W), .Output(bc_5_output));
  BC bc_6 (.Input(I1), .Clock(clock_1_out), .Enable(decoder_1_out1), .R___W(R_W), .Output(bc_6_output));
  BC bc_7 (.Input(I1), .Clock(clock_1_out), .Enable(decoder_1_out2), .R___W(R_W), .Output(bc_7_output));
  BC bc_8 (.Input(I1), .Clock(clock_1_out), .Enable(decoder_1_out3), .R___W(R_W), .Output(bc_8_output));
  or or_2 (or_2_out, bc_7_output, bc_6_output, bc_5_output, bc_8_output);
  and and_1 (O0, or_1_out, E);
  BC bc_9 (.Input(I2), .Clock(clock_1_out), .Enable(decoder_1_out0), .R___W(R_W), .Output(bc_9_output));
  BC bc_10 (.Input(I2), .Clock(clock_1_out), .Enable(decoder_1_out1), .R___W(R_W), .Output(bc_10_output));
  BC bc_11 (.Input(I2), .Clock(clock_1_out), .Enable(decoder_1_out2), .R___W(R_W), .Output(bc_11_output));
  BC bc_12 (.Input(I2), .Clock(clock_1_out), .Enable(decoder_1_out3), .R___W(R_W), .Output(bc_12_output));
  and and_2 (O1, or_2_out, E);
  BC bc_13 (.Input(I3), .Clock(clock_1_out), .Enable(decoder_1_out0), .R___W(R_W), .Output(bc_13_output));
  BC bc_14 (.Input(I3), .Clock(clock_1_out), .Enable(decoder_1_out1), .R___W(R_W), .Output(bc_14_output));
  BC bc_15 (.Input(I3), .Clock(clock_1_out), .Enable(decoder_1_out2), .R___W(R_W), .Output(bc_15_output));
  BC bc_16 (.Input(I3), .Clock(clock_1_out), .Enable(decoder_1_out3), .R___W(R_W), .Output(bc_16_output));
  or or_3 (or_3_out, bc_11_output, bc_10_output, bc_9_output, bc_12_output);
  and and_3 (O2, or_3_out, E);
  or or_4 (or_4_out, bc_16_output, bc_15_output, bc_14_output, bc_13_output);
  and and_4 (O3, or_4_out, E);
endmodule

module _32x4 (
  input  I0,
  input  I1,
  input  I2,
  input  I3,
  input  E,
  input  [4:0] Addr,
  input  R_W,
  output O0,
  output O1,
  output O2,
  output O3
);

  wire decoder_1_out0, decoder_1_out1, decoder_1_out2, decoder_1_out3, decoder_1_out4, decoder_1_out5,
       decoder_1_out6, decoder_1_out7, n4x4_1_o0, n4x4_1_o1, n4x4_1_o2, n4x4_1_o3, n4x4_2_o0, n4x4_2_o1,
       n4x4_2_o2, n4x4_2_o3, n4x4_3_o0, n4x4_3_o1, n4x4_3_o2, n4x4_3_o3, n4x4_4_o0, n4x4_4_o1, n4x4_4_o2,
       n4x4_4_o3, n4x4_5_o0, n4x4_5_o1, n4x4_5_o2, n4x4_5_o3, n4x4_6_o0, n4x4_6_o1, n4x4_6_o2, n4x4_6_o3,
       n4x4_7_o0, n4x4_7_o1, n4x4_7_o2, n4x4_7_o3, n4x4_8_o0, n4x4_8_o1, n4x4_8_o2, n4x4_8_o3, or_1_out,
       or_2_out, or_3_out, or_4_out;

  Decoder #(.select(3)) decoder_1 (
    .out0(decoder_1_out0), .out1(decoder_1_out1), .out2(decoder_1_out2), .out3(decoder_1_out3),
    .out4(decoder_1_out4), .out5(decoder_1_out5), .out6(decoder_1_out6), .out7(decoder_1_out7),
    .sel(Addr[4:2]), .en(E));
  _4x4 u_4x4_1 (
    .E(decoder_1_out0), .Addr(Addr[1:0]), .R_W(R_W), .I0(I0), .I1(I1), .I2(I2), .I3(I3), .O0(n4x4_1_o0),
    .O1(n4x4_1_o1), .O2(n4x4_1_o2), .O3(n4x4_1_o3));
  _4x4 u_4x4_2 (
    .E(decoder_1_out1), .Addr(Addr[1:0]), .R_W(R_W), .I0(I0), .I1(I1), .I2(I2), .I3(I3), .O0(n4x4_2_o0),
    .O1(n4x4_2_o1), .O2(n4x4_2_o2), .O3(n4x4_2_o3));
  _4x4 u_4x4_3 (
    .E(decoder_1_out2), .Addr(Addr[1:0]), .R_W(R_W), .I0(I0), .I1(I1), .I2(I2), .I3(I3), .O0(n4x4_3_o0),
    .O1(n4x4_3_o1), .O2(n4x4_3_o2), .O3(n4x4_3_o3));
  _4x4 u_4x4_4 (
    .E(decoder_1_out3), .Addr(Addr[1:0]), .R_W(R_W), .I0(I0), .I1(I1), .I2(I2), .I3(I3), .O0(n4x4_4_o0),
    .O1(n4x4_4_o1), .O2(n4x4_4_o2), .O3(n4x4_4_o3));
  _4x4 u_4x4_5 (
    .E(decoder_1_out4), .Addr(Addr[1:0]), .R_W(R_W), .I0(I0), .I1(I1), .I2(I2), .I3(I3), .O0(n4x4_5_o0),
    .O1(n4x4_5_o1), .O2(n4x4_5_o2), .O3(n4x4_5_o3));
  _4x4 u_4x4_6 (
    .E(decoder_1_out5), .Addr(Addr[1:0]), .R_W(R_W), .I0(I0), .I1(I1), .I2(I2), .I3(I3), .O0(n4x4_6_o0),
    .O1(n4x4_6_o1), .O2(n4x4_6_o2), .O3(n4x4_6_o3));
  _4x4 u_4x4_7 (
    .E(decoder_1_out6), .Addr(Addr[1:0]), .R_W(R_W), .I0(I0), .I1(I1), .I2(I2), .I3(I3), .O0(n4x4_7_o0),
    .O1(n4x4_7_o1), .O2(n4x4_7_o2), .O3(n4x4_7_o3));
  _4x4 u_4x4_8 (
    .E(decoder_1_out7), .Addr(Addr[1:0]), .R_W(R_W), .I0(I0), .I1(I1), .I2(I2), .I3(I3), .O0(n4x4_8_o0),
    .O1(n4x4_8_o1), .O2(n4x4_8_o2), .O3(n4x4_8_o3));
  or or_1 (or_1_out, n4x4_1_o0, n4x4_2_o0, n4x4_3_o0, n4x4_4_o0, n4x4_5_o0, n4x4_6_o0, n4x4_7_o0, n4x4_8_o0);
  or or_2 (or_2_out, n4x4_1_o1, n4x4_2_o1, n4x4_3_o1, n4x4_4_o1, n4x4_5_o1, n4x4_6_o1, n4x4_7_o1, n4x4_8_o1);
  or or_3 (or_3_out, n4x4_1_o2, n4x4_2_o2, n4x4_3_o2, n4x4_4_o2, n4x4_5_o2, n4x4_6_o2, n4x4_7_o2, n4x4_8_o2);
  or or_4 (or_4_out, n4x4_1_o3, n4x4_2_o3, n4x4_3_o3, n4x4_4_o3, n4x4_5_o3, n4x4_6_o3, n4x4_7_o3, n4x4_8_o3);
  and and_1 (O0, or_1_out, E);
  and and_2 (O1, or_2_out, E);
  and and_3 (O2, or_3_out, E);
  and and_4 (O3, or_4_out, E);
endmodule

module _256x4 (
  input  I0,
  input  I1,
  input  I2,
  input  I3,
  input  E,
  input  [7:0] Addr,
  input  R_W,
  output O0,
  output O1,
  output O2,
  output O3
);

  wire decoder_1_out0, decoder_1_out1, decoder_1_out2, decoder_1_out3, decoder_1_out4, decoder_1_out5,
       decoder_1_out6, decoder_1_out7, n32x4_1_o0, n32x4_1_o1, n32x4_1_o2, n32x4_1_o3, n32x4_2_o0,
       n32x4_2_o1, n32x4_2_o2, n32x4_2_o3, n32x4_3_o0, n32x4_3_o1, n32x4_3_o2, n32x4_3_o3, n32x4_4_o0,
       n32x4_4_o1, n32x4_4_o2, n32x4_4_o3, n32x4_5_o0, n32x4_5_o1, n32x4_5_o2, n32x4_5_o3, n32x4_6_o0,
       n32x4_6_o1, n32x4_6_o2, n32x4_6_o3, n32x4_7_o0, n32x4_7_o1, n32x4_7_o2, n32x4_7_o3, n32x4_8_o0,
       n32x4_8_o1, n32x4_8_o2, n32x4_8_o3, or_1_out, or_2_out, or_3_out, or_4_out;

  Decoder #(.select(3)) decoder_1 (
    .out0(decoder_1_out0), .out1(decoder_1_out1), .out2(decoder_1_out2), .out3(decoder_1_out3),
    .out4(decoder_1_out4), .out5(decoder_1_out5), .out6(decoder_1_out6), .out7(decoder_1_out7),
    .sel(Addr[7:5]), .en(E));
  _32x4 u_32x4_1 (
    .E(decoder_1_out0), .Addr(Addr[4:0]), .R_W(R_W), .I0(I0), .I1(I1), .I2(I2), .I3(I3), .O0(n32x4_1_o0),
    .O1(n32x4_1_o1), .O2(n32x4_1_o2), .O3(n32x4_1_o3));
  _32x4 u_32x4_2 (
    .E(decoder_1_out1), .Addr(Addr[4:0]), .R_W(R_W), .I0(I0), .I1(I1), .I2(I2), .I3(I3), .O0(n32x4_2_o0),
    .O1(n32x4_2_o1), .O2(n32x4_2_o2), .O3(n32x4_2_o3));
  _32x4 u_32x4_3 (
    .E(decoder_1_out2), .Addr(Addr[4:0]), .R_W(R_W), .I0(I0), .I1(I1), .I2(I2), .I3(I3), .O0(n32x4_3_o0),
    .O1(n32x4_3_o1), .O2(n32x4_3_o2), .O3(n32x4_3_o3));
  _32x4 u_32x4_4 (
    .E(decoder_1_out3), .Addr(Addr[4:0]), .R_W(R_W), .I0(I0), .I1(I1), .I2(I2), .I3(I3), .O0(n32x4_4_o0),
    .O1(n32x4_4_o1), .O2(n32x4_4_o2), .O3(n32x4_4_o3));
  _32x4 u_32x4_5 (
    .E(decoder_1_out4), .Addr(Addr[4:0]), .R_W(R_W), .I0(I0), .I1(I1), .I2(I2), .I3(I3), .O0(n32x4_5_o0),
    .O1(n32x4_5_o1), .O2(n32x4_5_o2), .O3(n32x4_5_o3));
  _32x4 u_32x4_6 (
    .E(decoder_1_out5), .Addr(Addr[4:0]), .R_W(R_W), .I0(I0), .I1(I1), .I2(I2), .I3(I3), .O0(n32x4_6_o0),
    .O1(n32x4_6_o1), .O2(n32x4_6_o2), .O3(n32x4_6_o3));
  _32x4 u_32x4_7 (
    .E(decoder_1_out6), .Addr(Addr[4:0]), .R_W(R_W), .I0(I0), .I1(I1), .I2(I2), .I3(I3), .O0(n32x4_7_o0),
    .O1(n32x4_7_o1), .O2(n32x4_7_o2), .O3(n32x4_7_o3));
  _32x4 u_32x4_8 (
    .E(decoder_1_out7), .Addr(Addr[4:0]), .R_W(R_W), .I0(I0), .I1(I1), .I2(I2), .I3(I3), .O0(n32x4_8_o0),
    .O1(n32x4_8_o1), .O2(n32x4_8_o2), .O3(n32x4_8_o3));
  or or_1 (or_1_out, n32x4_1_o0, n32x4_2_o0, n32x4_3_o0, n32x4_4_o0, n32x4_5_o0, n32x4_6_o0, n32x4_7_o0, n32x4_8_o0);
  or or_2 (or_2_out, n32x4_1_o1, n32x4_2_o1, n32x4_3_o1, n32x4_4_o1, n32x4_5_o1, n32x4_6_o1, n32x4_7_o1, n32x4_8_o1);
  or or_3 (or_3_out, n32x4_1_o2, n32x4_2_o2, n32x4_3_o2, n32x4_4_o2, n32x4_5_o2, n32x4_6_o2, n32x4_7_o2, n32x4_8_o2);
  or or_4 (or_4_out, n32x4_1_o3, n32x4_2_o3, n32x4_3_o3, n32x4_4_o3, n32x4_5_o3, n32x4_6_o3, n32x4_7_o3, n32x4_8_o3);
  and and_1 (O0, or_1_out, E);
  and and_2 (O1, or_2_out, E);
  and and_3 (O2, or_3_out, E);
  and and_4 (O3, or_4_out, E);
endmodule

module Input (
  input  [3:0] A,
  input  [3:0] B,
  input  Addr_Enable,
  input  DataSwitch,
  output [3:0] Data,
  output [7:0] Address
);

  wire [7:0] adder_1_out, AddressGen_out;

  Random AddressGen (.clk(Addr_Enable), .out(AddressGen_out));  // open: next, clr
  Adder adder_1 (.a(AddressGen_out), .b(8'h1), .out(adder_1_out));  // open: cin, cout
  Multiplexer #(.width(4), .enable("false")) multiplexer_1 (.in0(A), .in1(B), .out(Data), .sel(DataSwitch));
  Multiplexer #(.width(8), .enable("false")) multiplexer_2 (
    .in0(AddressGen_out), .in1(adder_1_out), .out(Address), .sel(DataSwitch));
endmodule

module ALU (
  input  [3:0] A,
  input  Enable,
  input  [3:0] B,
  input  [1:0] Select,
  output Overflow,
  output [3:0] Output,
  output [3:0] MulCarryOut
);

  wire adder_1_cout, subtractor_1_bout;
  wire [3:0] adder_1_out, multiplier_1_cout, multiplier_1_out, or_1_out, subtractor_1_out;

  Adder #(.width(4)) adder_1 (.a(A), .b(B), .out(adder_1_out), .cout(adder_1_cout));  // open: cin
  Subtractor #(.width(4)) subtractor_1 (.a(A), .b(B), .out(subtractor_1_out), .bout(subtractor_1_bout));  // open: bin
  assign or_1_out = A | B;  // OR_Gate or_1, 4 bits wide
  Multiplier #(.width(4)) multiplier_1 (.a(A), .b(B), .out(multiplier_1_out), .cout(multiplier_1_cout));  // open: cin
  Multiplexer #(.select(2)) multiplexer_1 (
    .in0(adder_1_cout), .in1(subtractor_1_bout), .out(Overflow), .sel(Select), .en(Enable));  // open: in2, in3
  Multiplexer #(.select(2), .width(4)) multiplexer_2 (
    .in0(adder_1_out), .in1(subtractor_1_out), .in2(or_1_out), .in3(multiplier_1_out), .out(Output),
    .sel(Select), .en(Enable));
  Demultiplexer #(.select(2), .width(4)) demultiplexer_1 (
    .out3(MulCarryOut), .in(multiplier_1_cout), .sel(Select), .en(Enable));  // open: out0, out1, out2
endmodule

module Output (
  input  [3:0] in_1,
  output a,
  output out_3,
  output out_4,
  output out_5,
  output out_6,
  output out_7,
  output out_8
);

  // Display display_1: pin names not known; wires that end beside it: in_1[3], in_1[2], in_1[1], in_1[0], a, out_3, out_4, out_5, out_6, out_7, out_8
  _7_Segment_Display u_7_segment_display_1 (
    .g(out_8), .f(out_7), .a(a), .b(out_3), .e(out_6), .d(out_5), .c(out_4));  // open: dp
endmodule

module Main (
  input  [3:0] A,
  input  [3:0] B,
  input  Enable,
  input  Load_B,
  input  [1:0] L___F,
  input  [1:0] OP_code,
  output Overflow,
  output [3:0] Output,
  output [3:0] MulCarryOut
);

  wire and_1_out, and_2_out, and_3_out, clk_out, not_1_out, not_2_out, not_3_out, Read_Write_out;
  wire [3:0] alu_1_output, Data_A_q, Data_B_q, demultiplexer_1_out1, demultiplexer_1_out2, input_1_data,
       n256x4_1_o3;
  wire [7:0] input_1_address, multiplexer_1_out, REG1_q, REG2_q;

  Input input_1 (
    .A(A), .B(B), .Addr_Enable(Enable), .DataSwitch(Load_B), .Data(input_1_data), .Address(input_1_address));
  not not_1 (not_1_out, Load_B);
  Clock clk (.out(clk_out));
  Register REG2 (.D(input_1_address), .en(Load_B), .Q(REG2_q), .clk(clk_out));  // open: clr
  Register REG1 (.D(input_1_address), .en(not_1_out), .Q(REG1_q), .clk(clk_out));  // open: clr
  Multiplexer #(.select(2), .width(8), .enable("false")) multiplexer_1 (
    .in0(input_1_address), .in1(REG1_q), .in2(REG2_q), .out(multiplexer_1_out), .sel(L___F));  // open: in3
  xor Read_Write (Read_Write_out, L___F[0], L___F[1]);
  and and_1 (and_1_out, L___F[0], L___F[1]);
  not not_2 (not_2_out, L___F[0]);
  not not_3 (not_3_out, L___F[1]);
  _256x4 u_256x4_1 (
    .E(Enable), .Addr(multiplexer_1_out), .R_W(Read_Write_out), .I0(input_1_data[3]), .I1(input_1_data[2]),
    .I2(input_1_data[1]), .I3(input_1_data[0]), .O0(n256x4_1_o3[3]), .O1(n256x4_1_o3[2]),
    .O2(n256x4_1_o3[1]), .O3(n256x4_1_o3[0]));
  Demultiplexer #(.select(2), .width(4), .enable("false")) demultiplexer_1 (
    .out1(demultiplexer_1_out1), .out2(demultiplexer_1_out2), .in(n256x4_1_o3), .sel(L___F));  // open: out0, out3
  and and_2 (and_2_out, L___F[1], not_2_out);
  and and_3 (and_3_out, L___F[0], not_3_out);
  Register #(.width(4)) Data_A (.D(demultiplexer_1_out1), .en(and_3_out), .Q(Data_A_q), .clk(clk_out));  // open: clr
  Register #(.width(4)) Data_B (.D(demultiplexer_1_out2), .en(and_2_out), .Q(Data_B_q), .clk(clk_out));  // open: clr
  ALU alu_1 (
    .A(Data_A_q), .B(Data_B_q), .Select(OP_code), .Enable(and_1_out), .Overflow(Overflow),
    .Output(alu_1_output), .MulCarryOut(MulCarryOut));
  Multiplexer #(.select(2), .width(4), .enable("false")) multiplexer_2 (
    .in0(n256x4_1_o3), .in1(n256x4_1_o3), .in2(n256x4_1_o3), .in3(alu_1_output), .out(Output), .sel(L___F));
  Hex_Digit_Display hex_digit_display_1 (.value(Output));  // open: dp
endmodule

module CPU (
  input  [3:0] A,
  input  [3:0] B,
  input  Power,
  output [1:0] out_4,
  output [1:0] out_5
);

  wire L_F_Control_out, Load_out, main_1_overflow, OperationControl_out;
  wire [3:0] main_1_mulcarryout, main_1_output;

  Button_part Load (.out(Load_out));
  Button_part L_F_Control (.out(L_F_Control_out));
  Button_part OperationControl (.out(OperationControl_out));
  Button button_1 (.ButtonPress(L_F_Control_out), .Out(out_5));
  Button button_2 (.ButtonPress(OperationControl_out), .Out(out_4));
  Main main_1 (
    .A(A), .B(B), .Enable(Power), .Load_B(Load_out), .OP_code(out_4), .L___F(out_5),
    .Overflow(main_1_overflow), .Output(main_1_output), .MulCarryOut(main_1_mulcarryout));
  LED Overflow (.in(main_1_overflow));
  Hex_Digit_Display hex_digit_display_1 (.value(main_1_mulcarryout));  // open: dp
  Hex_Digit_Display hex_digit_display_2 (.value(main_1_output));  // open: dp

  // Notes on the sheet:
  //   00 - LOAD
  //   01 - FETCH A
  //   10 - FETCH B
  //   11 - OPERATIONS
  //   Result
  //   MulCarry
  //   00 - ADD
  //   01 - SUB
  //   10 - OR
  //   11 - MULTIPLY
  //   Result - Operation Output
  //   MulCarry - Carry from Multiplication Operation
endmodule

module Button (
  input  ButtonPress,
  output [1:0] Out
);

  Counter #(.width(2), .max('h3)) counter_1 (.Q(Out), .clk(ButtonPress));  // open: load, D, count, carry, clr
endmodule
