// Logisim project test.circ as structural Verilog: 1 circuit, main circuit main
module main (
  input  [3:0] Data,
  input  Set_A,
  input  Set_B,
  input  Set_O,
  input  Reset,
  output [3:0] Output,
  output Overflow
);

  wire [3:0] adder_1_out, and_1_out, multiplier_1_cout, multiplier_1_out, not_1_out, not_2_out, or_1_out,
       register_1_q, register_2_q, register_3_q, shifter_1_out, shifter_2_out, xor_1_out;

  Register #(.width(4)) register_1 (.D(Data), .Q(register_1_q), .clk(Set_A), .clr(Reset));  // open: en
  Register #(.width(4)) register_2 (.D(Data), .Q(register_2_q), .clk(Set_B), .clr(Reset));  // open: en
  Register #(.width(4)) register_3 (.D(Data), .Q(register_3_q), .clk(Set_O), .clr(Reset));  // open: en
  assign not_1_out = ~register_1_q;  // NOT_Gate not_1, 4 bits wide
  assign not_2_out = ~register_2_q;  // NOT_Gate not_2, 4 bits wide
  assign or_1_out = register_1_q | register_2_q;  // OR_Gate or_1, 4 bits wide
  assign and_1_out = register_1_q & register_2_q;  // AND_Gate and_1, 4 bits wide
  assign xor_1_out = register_1_q ^ register_2_q;  // XOR_Gate xor_1, 4 bits wide
  Adder #(.width(4)) adder_1 (.a(register_1_q), .b(register_2_q), .out(adder_1_out), .cout(Overflow));  // open: cin
  Multiplier #(.width(4)) multiplier_1 (
    .a(register_1_q), .b(register_2_q), .out(multiplier_1_out), .cout(multiplier_1_cout));  // open: cin
  Shifter #(.width(4)) shifter_1 (.in(register_1_q), .\dist (register_2_q[1:0]), .out(shifter_1_out));
  Shifter #(.width(4), .shift("lr")) shifter_2 (.in(register_1_q), .\dist (register_2_q[1:0]), .out(shifter_2_out));
  Multiplexer #(.select(4), .width(4), .enable("false")) multiplexer_1 (
    .in0(register_1_q), .in1(register_2_q), .in2(not_1_out), .in3(not_2_out), .in4(or_1_out),
    .in5(and_1_out), .in6(xor_1_out), .in7(adder_1_out), .in8(multiplier_1_out), .in9(multiplier_1_cout),
    .in10(shifter_1_out), .in11(shifter_2_out), .out(Output), .sel(register_3_q));  // open: in12, in13, in14, in15
endmodule
